// Logisim project aois4.circ as structural Verilog: 2 circuits, main circuit main
module main (
  input  in_1,
  input  in_2,
  input  in_3,
  output out_4,
  output out_5
);

  wire and_1_out, and_2_out, and_3_out, and_4_out, and_5_out, and_6_out, and_7_out, not_1_out, not_2_out,
       not_3_out;

  not not_1 (not_1_out, in_1);
  not not_2 (not_2_out, in_2);
  not not_3 (not_3_out, in_3);
  and and_1 (and_1_out, not_1_out, not_2_out, in_3);
  and and_2 (and_2_out, not_1_out, in_2, not_3_out);
  and and_3 (and_3_out, in_1, not_2_out, not_3_out);
  and and_4 (and_4_out, in_1, in_2, in_3);
  and and_5 (and_5_out, not_1_out, in_3);
  and and_6 (and_6_out, not_1_out, in_2);
  and and_7 (and_7_out, in_2, in_3);
  or or_1 (out_4, and_1_out, and_2_out, and_3_out, and_4_out);
  or or_2 (out_5, and_5_out, and_6_out, and_7_out);
endmodule

module d8421 (
  input  X1,
  input  X2,
  input  X3,
  input  X4,
  output [3:0] out_5
);

  wire not_1_out, not_2_out, not_3_out, not_4_out;

  not not_1 (not_1_out, X1);
  not not_2 (not_2_out, X2);
  not not_3 (not_3_out, X3);
  not not_4 (not_4_out, X4);
  or or_1 (out_5[3], X2, X1);
  buf or_2 (out_5[2], not_2_out);  // OR_Gate
  buf or_3 (out_5[1], X3);  // OR_Gate
  buf or_4 (out_5[0], X4);  // OR_Gate
endmodule
